# Fritzing sketch access_control_module (saved by Fritzing 0.9.3b)
circuit board: 10cm x 5cm
breadboards: 1

parts:
  ESP8266 = female pin header, 15 pins [form="♀ (female)"]
  ESP8266_2 = female pin header, 15 pins [form="♀ (female)"]
  J3 = female pin header, 10 pins [form="♀ (female)"]  # not connected
  HLK-PM01 = HLK-PM01
  OUT = Screw terminal - 2 pins [package=THT]
  BC547 = TRANSISTOR_NPN [package=to-92-ammo]
  1KΩ = Resistor [tolerance=±5% resistance=1k package=THT]
  47µF = Electrolytic Capacitor [capacitance=47µF voltage=50V package="100 mil [THT, electrolytic]"]
  10KΩ = Resistor [tolerance=±5% resistance=10k package=THT]
  LOCK_POW_IN = Screw terminal - 2 pins [package=THT]
  RELAY = OMRON PCB Power Relay – G5LE [part_number="G5LE-1\n" package=THT]
  ledBeep1 = Screw terminal - 2 pins [package=THT]
  power1 = Screw terminal - 2 pins [package=THT]
  Data1 = Screw terminal - 2 pins [package=THT]
  ledBeep2 = Screw terminal - 2 pins [package=THT]
  Data2 = Screw terminal - 2 pins [package=THT]
  power2 = Screw terminal - 2 pins [package=THT]
  AC_MAINS_IN = Screw terminal - 2 pins [package=THT]
  R1 = Resistor [tolerance=±5% resistance=220 package=THT]

nets:
  N1: ESP8266.pin15, HLK-PM01.+Vo, 47µF.+, RELAY.COIL2, power1.pin2, power2.pin2
  N2: ESP8266_2.pin1, 1KΩ.Pin_0
  N3: ESP8266_2.pin2, ledBeep2.pin1
  N4: ESP8266_2.pin3, ledBeep2.pin2
  N5: ESP8266_2.pin4, Data2.pin1
  N6: ESP8266_2.pin5, Data2.pin2
  N7: ESP8266_2.pin8, ledBeep1.pin1
  N8: ESP8266_2.pin9, Data1.pin1
  N9: ESP8266_2.pin10, Data1.pin2
  N10: ESP8266_2.pin11, ledBeep1.pin2, R1.Pin_1
  N11: ESP8266_2.pin14, R1.Pin_0
  N12: HLK-PM01.AC#0, AC_MAINS_IN.pin1
  N13: HLK-PM01.AC#1, AC_MAINS_IN.pin2
  N14: HLK-PM01.-Vo, BC547.C, 47µF.-, 10KΩ.Pin_1, power1.pin1, power2.pin1
  N15: OUT.pin1, LOCK_POW_IN.pin1
  N16: OUT.pin2, RELAY.A
  N17: BC547.E, RELAY.COIL1
  N18: BC547.B, 1KΩ.Pin_1, 10KΩ.Pin_0
  N19: LOCK_POW_IN.pin2, RELAY.C

notes:
  VCC
  GND
  DATA0
  DATA1
  BEEP
  LED
  ENTER
  EXIT
  5V
